# Fritzing sketch relierv2_production (saved by Fritzing 0.9.3b)
circuit board: 8.31cm x 5.2cm
breadboards: 2

parts:
  40pines_RPi3 = Raspberry Pi Header 40pin [form="♂ (male)" package=THT]
  10k = Resistor [tolerance=±0.1% resistance=10k package=THT]
  10k_2 = Resistor [tolerance=±0.1% resistance=10k package=THT]
  20k = Resistor [tolerance=±1% resistance=20k package=THT]
  RGB_led = RGB LED - (4 legs) [package="5 mm [THT]"]
  220Ω = Resistor [tolerance=±0.1% resistance=220 package=THT]
  220Ω_2 = Resistor [tolerance=±0.1% resistance=220 package=THT]
  220Ω_3 = Resistor [tolerance=±0.1% resistance=150 package=THT]
  Pi = Dagu DGServo 9g header (male) [package=THT]
  Turb = Dagu DGServo 9g header (male) [package=THT]
  Pd = Dagu DGServo 9g header (male) [package=THT]
  Button = male pin header, 2 pins [form="♂ (male)"]
  WTemp = Dagu DGServo 9g header (male) [package=THT]
  Flow = Dagu DGServo 9g header (male) [package=THT]
  Pu = Dagu DGServo 9g header (male) [package=THT]
  Logic_Level_Converter = Logic Level Converter [package="Breakout board"]
  ADC_ADS1115 = Adafruit ADS1115 16Bit I2C ADC [part_number="Adafruit #1085"]
  Nextion = male pin header, 4 pins [form="♂ (male)" part_number=Nextion]
  GND/GPIO6/13 = Dagu DGServo 9g header (male) [package=THT]
  GND/3_3/5V = Dagu DGServo 9g header (male) [package=THT]
  BME280 = Barometric Pressure Sensor - BMP180 Breakout (GY-68)
  Button_2 = Round Pushbutton  # not connected
  Buzzer = Buzzer 12mm [package=buzzer-12mm-ns-kit]

nets:
  3.3v: 40pines_RPi3.3v3, 40pines_RPi3.3V3, 10k.Pin_1, WTemp.Vcc, Logic_Level_Converter.LV, GND/3_3/5V.Vcc, BME280.VCC
  N1: 40pines_RPi3.GPIO2, Logic_Level_Converter.LV2, BME280.SDA
  N2: 40pines_RPi3.GPIO3, Logic_Level_Converter.LV1, BME280.SCL
  GPIO4: 40pines_RPi3.GIPO4, 10k.Pin_0, WTemp.pulse
  ground: 40pines_RPi3.GND, 20k.Pin_0, RGB_led.common_anode, Pi.gnd, Turb.gnd, Pd.gnd, Button.pin2, WTemp.gnd, Flow.gnd, Pu.gnd, Logic_Level_Converter.L-GND, Logic_Level_Converter.H-GND, ADC_ADS1115.GND, Nextion.pin4, GND/GPIO6/13.gnd, GND/3_3/5V.gnd, BME280.GND, Buzzer.2
  GPIO17: 40pines_RPi3.GIPO17, Button.pin1
  GPIO27: 40pines_RPi3.GIPO27, 10k_2.Pin_0, 20k.Pin_1
  N3: 40pines_RPi3.GIPO6, GND/GPIO6/13.Vcc
  N4: 40pines_RPi3.GIPO13, GND/GPIO6/13.pulse
  N5: 40pines_RPi3.GIPO26, 220Ω.Pin_0
  N6: 40pines_RPi3.GIPO21, 220Ω_2.Pin_0
  N7: 40pines_RPi3.GIPO16, 220Ω_3.Pin_0
  GPIO18: 40pines_RPi3.GIPO18, Buzzer.1
  N8: 40pines_RPi3.GIPO15, Nextion.pin2
  N9: 40pines_RPi3.GIPO14, Nextion.pin3
  5V: 40pines_RPi3.5V, Pi.Vcc, Turb.Vcc, Pd.Vcc, Flow.Vcc, Pu.Vcc, Logic_Level_Converter.HV, ADC_ADS1115.VDD, Nextion.pin1, GND/3_3/5V.pulse
  N10: 10k_2.Pin_1, Flow.pulse
  N11: RGB_led.red_cathode, 220Ω_3.Pin_1
  N12: RGB_led.green_cathode, 220Ω_2.Pin_1
  N13: RGB_led.blue_cathode, 220Ω.Pin_1
  N14: Pi.pulse, ADC_ADS1115.AIN1
  N15: Turb.pulse, ADC_ADS1115.AIN3
  N16: Pd.pulse, ADC_ADS1115.AIN2
  N17: Pu.pulse, ADC_ADS1115.AIN0
  N18: Logic_Level_Converter.HV2, ADC_ADS1115.SDA
  N19: Logic_Level_Converter.HV1, ADC_ADS1115.SCL

notes:
  relier AS
  Ricardos@lnec.pt
  Ricardos.geral@gmail.com
  Ricardo
  dos Santos
  v2 - 2018
  github.com/Ricardosgeral/relier
  Github project: github.com/Ricardosgeral/relier
  Project webpage: ricardosgeral.github.io/relier
  (.)(.)
  Ricardo dos Santos 2018

custom parts:
  Raspberry Pi Header 40pin: Raspberry Pi 40 pin header - for creating your own shields.
  Logic Level Converter: 5V to/from 3.3V logic level converter
  Adafruit ADS1115 16Bit I2C ADC: For microcontrollers without an analog-to-digital converter or when you want a higher-precision ADC, the ADS1115 provides 16-bit precision at 860 samples/second over I2C. The chip can be configured as 4 single-ended input channels, or two differential channels. As a nice bonus, it even includes a programmable gain amplifier, up to x16, to help boost up smaller single/differential signals to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
