# Fritzing sketch relierv3.2_production(hat) (saved by Fritzing 0.9.3b)
circuit board: 6.50001cm x 8.29998cm
breadboards: 2

parts:
  40pines_RPi3B = Raspberry Pi Header 40pin [form="♂ (male)" package=THT]
  Logic_Level_Converter = Logic Level Converter [package="Breakout board"]
  ADC_ADS1116 = Adafruit ADS1115 16Bit I2C ADC [part_number="Adafruit #1085"]
  WTemp = Dagu DGServo 9g header (male) [package=THT]
  Flow = Dagu DGServo 9g header (male) [package=THT]
  Turb = Dagu DGServo 9g header (male) [package=THT]
  Pd = Dagu DGServo 9g header (male) [package=THT]
  Pi = Dagu DGServo 9g header (male) [package=THT]
  Pu = Dagu DGServo 9g header (male) [package=THT]
  Nextion = male pin header, 4 pins [form="♂ (male)"]
  20kΩ = Resistor [tolerance=±1% resistance=20k package=THT]
  10kΩ = Resistor [tolerance=±0.1% resistance=10k package=THT]
  Buzzer = Buzzer 12mm [package=buzzer-12mm-ns-kit]
  BME280 = Barometric Pressure Sensor - BMP180 Breakout (GY-68)
  GND/5v/3_3v = Dagu DGServo 9g header (male) [package=THT]
  GND/GPIO26/19 = Dagu DGServo 9g header (male) [package=THT]
  RGB_led = RGB LED - (4 legs) [package="5 mm [THT]"]
  Button = Round Pushbutton
  220Ω = Resistor [tolerance=±0.1% resistance=220 package=THT]
  220Ω_2 = Resistor [tolerance=±0.1% resistance=220 package=THT]
  220Ω_3 = Resistor [tolerance=±0.1% resistance=220 package=THT]
  10kΩ_2 = Resistor [tolerance=±0.1% resistance=10k package=THT]
  pull-up_trb = Resistor [tolerance=±1% resistance=330k package="0805 [SMD]"]
  pull-up_dwn = Resistor [tolerance=±1% resistance=330k package="0805 [SMD]"]
  pull-up_int = Resistor [tolerance=±1% resistance=330k package="0805 [SMD]"]
  pull-up_pu = Resistor [tolerance=±1% resistance=330k package="0805 [SMD]"]

nets:
  3.3V: 40pines_RPi3B.3v3, 40pines_RPi3B.3V3, Logic_Level_Converter.LV, WTemp.Vcc, 10kΩ.Pin_0, BME280.VCC, GND/5v/3_3v.pulse
  SDA_l: 40pines_RPi3B.GPIO2, Logic_Level_Converter.LV2, BME280.SDA
  SCL_l: 40pines_RPi3B.GPIO3, Logic_Level_Converter.LV1, BME280.SCL
  GND: 40pines_RPi3B.GND, Logic_Level_Converter.L-GND, Logic_Level_Converter.H-GND, ADC_ADS1116.GND, WTemp.gnd, Flow.gnd, Turb.gnd, Pd.gnd, Pi.gnd, Pu.gnd, Nextion.pin1, 20kΩ.Pin_0, Buzzer.2, BME280.GND, GND/5v/3_3v.gnd, GND/GPIO26/19.gnd, RGB_led.common_anode, Button.leg0
  GPIO19: 40pines_RPi3B.GIPO19, GND/GPIO26/19.pulse
  GPIO26: 40pines_RPi3B.GIPO26, GND/GPIO26/19.Vcc
  GPIO21: 40pines_RPi3B.GIPO21, 220Ω.Pin_0
  GPIO16: 40pines_RPi3B.GIPO16, 220Ω_2.Pin_0
  GPIO12: 40pines_RPi3B.GIPO12, 220Ω_3.Pin_0
  GPIO25: 40pines_RPi3B.GIPO25, 20kΩ.Pin_1, 10kΩ_2.Pin_0
  GPIO24: 40pines_RPi3B.GIPO24, WTemp.pulse, 10kΩ.Pin_1
  GPIO23: 40pines_RPi3B.GIPO23, Button.leg1
  GPIO18: 40pines_RPi3B.GIPO18, Buzzer.1
  Rx-Tx: 40pines_RPi3B.GIPO15, Nextion.pin3
  Tx-Rx: 40pines_RPi3B.GIPO14, Nextion.pin2
  5V: 40pines_RPi3B.5V, Logic_Level_Converter.HV, ADC_ADS1116.VDD, Flow.Vcc, Turb.Vcc, Pd.Vcc, Pi.Vcc, Pu.Vcc, Nextion.pin4, GND/5v/3_3v.Vcc, pull-up_trb.Pin_1, pull-up_dwn.Pin_1, pull-up_int.Pin_1, pull-up_pu.Pin_1
  SDA_h: Logic_Level_Converter.HV2, ADC_ADS1116.SDA
  SCL_h: Logic_Level_Converter.HV1, ADC_ADS1116.SCL
  ana3: ADC_ADS1116.AIN3, Turb.pulse, pull-up_trb.Pin_0
  ana2: ADC_ADS1116.AIN2, Pd.pulse, pull-up_dwn.Pin_0
  ana1: ADC_ADS1116.AIN1, Pi.pulse, pull-up_int.Pin_0
  ana0: ADC_ADS1116.AIN0, Pu.pulse, pull-up_pu.Pin_0
  N1: Flow.pulse, 10kΩ_2.Pin_1
  N2: RGB_led.red_cathode, 220Ω_2.Pin_1
  N3: RGB_led.green_cathode, 220Ω.Pin_1
  N4: RGB_led.blue_cathode, 220Ω_3.Pin_1

notes:
  Ricardo dos Santos 2018
  github.com/Ricardosgeral/relier
  Ricardos.geral@gmail.com
  Ricardos@lnec.pt
  v3.1 - Oct2018
  relier AS - hat
  Ricardo dos Santos
  relier AS hat
  v3.2 nov 2018
  Project repository:
  330kΩ

custom parts:
  Raspberry Pi Header 40pin: Raspberry Pi 40 pin header - for creating your own shields.
  Logic Level Converter: 5V to/from 3.3V logic level converter
  Adafruit ADS1115 16Bit I2C ADC: For microcontrollers without an analog-to-digital converter or when you want a higher-precision ADC, the ADS1115 provides 16-bit precision at 860 samples/second over I2C. The chip can be configured as 4 single-ended input channels, or two differential channels. As a nice bonus, it even includes a programmable gain amplifier, up to x16, to help boost up smaller single/differential signals to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
